// Logisim project S1-T8.circ as structural Verilog: 10 circuits, main circuit Main
module condition1 (
  input  R1,
  input  G1,
  input  R1_2,
  input  G2,
  input  R3,
  input  G3,
  output _1,
  output _2,
  output _3
);

  wire nor_1_out, nor_2_out, nor_3_out;

  nor nor_1 (nor_1_out, R1, R1, R1, G1, G1);
  nor nor_2 (nor_2_out, R1_2, R1_2, G2, G2, G2);
  nor nor_3 (nor_3_out, R3, R3, R3, G3, G3);
  and and_1 (_1, nor_1_out, G2, G3);
  and and_2 (_2, G1, nor_2_out, G3);
  and and_3 (_3, G1, G2, nor_3_out);

  // Notes on the sheet:
  //   CONDITION 1
endmodule

module decision1 (
  input  R1,
  input  G1,
  input  R2,
  input  G2,
  input  R3,
  input  G3,
  input  R4,
  input  G4,
  input  R5,
  input  G5,
  input  R6,
  input  G6,
  input  R7,
  input  G7,
  input  R8,
  input  G8,
  input  R9,
  input  G9,
  output _1,
  output _2,
  output _3,
  output _4,
  output _5,
  output _6,
  output _7,
  output _8,
  output _9
);

  wire condition1_1__1, condition1_1__2, condition1_1__3, condition1_2__1, condition1_2__2, condition1_2__3,
       condition1_3__1, condition1_3__2, condition1_3__3, condition1_4__1, condition1_4__2, condition1_4__3,
       condition1_5__1, condition1_5__2, condition1_5__3, condition1_6__1, condition1_6__2, condition1_6__3,
       condition1_7__1, condition1_7__2, condition1_7__3, condition1_8__1, condition1_8__2, condition1_8__3;

  condition1 condition1_1 (
    .R1(R1), .G1(G1), .R1_2(R2), .G2(G2), .R3(R3), .G3(G3), ._1(condition1_1__1), ._2(condition1_1__2),
    ._3(condition1_1__3));
  condition1 condition1_2 (
    .R1(R4), .G1(G4), .R1_2(R5), .G2(G5), .R3(R6), .G3(G6), ._1(condition1_2__1), ._2(condition1_2__2),
    ._3(condition1_2__3));
  condition1 condition1_3 (
    .R1(R7), .G1(G7), .R1_2(R8), .G2(G8), .R3(R9), .G3(G9), ._1(condition1_3__1), ._2(condition1_3__2),
    ._3(condition1_3__3));
  condition1 condition1_4 (
    .R1(R1), .G1(G1), .R1_2(R4), .G2(G4), .R3(R7), .G3(G7), ._1(condition1_4__1), ._2(condition1_4__2),
    ._3(condition1_4__3));
  condition1 condition1_5 (
    .R1(R2), .G1(G2), .R1_2(R5), .G2(G5), .R3(R8), .G3(G8), ._1(condition1_5__1), ._2(condition1_5__2),
    ._3(condition1_5__3));
  condition1 condition1_6 (
    .R1(R3), .G1(G3), .R1_2(R6), .G2(G6), .R3(R9), .G3(G9), ._1(condition1_6__1), ._2(condition1_6__2),
    ._3(condition1_6__3));
  condition1 condition1_7 (
    .R1(R1), .G1(G1), .R1_2(R5), .G2(G5), .R3(R9), .G3(G9), ._1(condition1_7__1), ._2(condition1_7__2),
    ._3(condition1_7__3));
  condition1 condition1_8 (
    .R1(R3), .G1(G3), .R1_2(R5), .G2(G5), .R3(R7), .G3(G7), ._1(condition1_8__1), ._2(condition1_8__2),
    ._3(condition1_8__3));
  or or_1 (_1, condition1_1__1, condition1_4__1, condition1_7__1);
  or or_2 (_2, condition1_1__2, condition1_5__1);
  or or_3 (_3, condition1_1__3, condition1_6__1, condition1_8__1);
  or or_4 (_4, condition1_2__1, condition1_4__2);
  or or_5 (_5, condition1_8__2, condition1_5__2, condition1_7__2, condition1_2__2);
  or or_6 (_6, condition1_2__3, condition1_6__2);
  or or_7 (_7, condition1_3__1, condition1_4__3, condition1_8__3);
  or or_8 (_8, condition1_3__2, condition1_5__3);
  or or_9 (_9, condition1_3__3, condition1_6__3, condition1_7__3);

  // Notes on the sheet:
  //   DECISION 1
endmodule

module condition2 (
  input  R1,
  input  G1,
  input  R2,
  input  G2,
  input  R3,
  input  G3,
  output _1,
  output _2,
  output _3
);

  wire nor_1_out, nor_2_out, nor_3_out;

  nor nor_1 (nor_1_out, R1, G1);
  nor nor_2 (nor_2_out, R2, G2);
  nor nor_3 (nor_3_out, R3, G3);
  and and_1 (_1, nor_1_out, R2, R3);
  and and_2 (_2, nor_2_out, R1, R3);
  and and_3 (_3, R1, nor_3_out, R2);

  // Notes on the sheet:
  //   CONDITION 2
endmodule

module decision2 (
  input  R1,
  input  G1,
  input  R2,
  input  G2,
  input  R3,
  input  G3,
  input  R4,
  input  G4,
  input  R5,
  input  G5,
  input  R6,
  input  G6,
  input  R7,
  input  G7,
  input  R8,
  input  G8,
  input  R9,
  input  G9,
  output _1,
  output _2,
  output _3,
  output _4,
  output _5,
  output _6,
  output _7,
  output _8,
  output _9
);

  wire condition2_1__1, condition2_1__2, condition2_1__3, condition2_2__1, condition2_2__2, condition2_2__3,
       condition2_3__1, condition2_3__2, condition2_3__3, condition2_4__1, condition2_4__2, condition2_4__3,
       condition2_5__1, condition2_5__2, condition2_5__3, condition2_6__1, condition2_6__2, condition2_6__3,
       condition2_7__1, condition2_7__2, condition2_7__3, condition2_8__1, condition2_8__2, condition2_8__3;

  condition2 condition2_1 (
    .R1(R1), .G1(G1), .R2(R2), .G2(G2), .R3(R3), .G3(G3), ._1(condition2_1__1), ._2(condition2_1__2),
    ._3(condition2_1__3));
  condition2 condition2_2 (
    .R1(R4), .G1(G4), .R2(R5), .G2(G5), .R3(R6), .G3(G6), ._1(condition2_2__1), ._2(condition2_2__2),
    ._3(condition2_2__3));
  condition2 condition2_3 (
    .R1(R7), .G1(G7), .R2(R8), .G2(G8), .R3(R9), .G3(G9), ._1(condition2_3__1), ._2(condition2_3__2),
    ._3(condition2_3__3));
  condition2 condition2_4 (
    .R1(R1), .G1(G1), .R2(R4), .G2(G4), .R3(R7), .G3(G7), ._1(condition2_4__1), ._2(condition2_4__2),
    ._3(condition2_4__3));
  condition2 condition2_5 (
    .R1(R2), .G1(G2), .R2(R5), .G2(G5), .R3(R8), .G3(G8), ._1(condition2_5__1), ._2(condition2_5__2),
    ._3(condition2_5__3));
  condition2 condition2_6 (
    .R1(R3), .G1(G3), .R2(R6), .G2(G6), .R3(R9), .G3(G9), ._1(condition2_6__1), ._2(condition2_6__2),
    ._3(condition2_6__3));
  condition2 condition2_7 (
    .R1(R1), .G1(G1), .R2(R5), .G2(G5), .R3(R9), .G3(G9), ._1(condition2_7__1), ._2(condition2_7__2),
    ._3(condition2_7__3));
  condition2 condition2_8 (
    .R1(R3), .G1(G3), .R2(R5), .G2(G5), .R3(R7), .G3(G7), ._1(condition2_8__1), ._2(condition2_8__2),
    ._3(condition2_8__3));
  or or_1 (_1, condition2_1__1, condition2_4__1, condition2_7__1);
  or or_2 (_2, condition2_1__2, condition2_5__1);
  or or_3 (_3, condition2_1__3, condition2_6__1, condition2_8__1);
  or or_4 (_4, condition2_2__1, condition2_4__2);
  or or_5 (_5, condition2_8__2, condition2_5__2, condition2_7__2, condition2_2__2);
  or or_6 (_6, condition2_2__3, condition2_6__2);
  or or_7 (_7, condition2_3__1, condition2_4__3, condition2_8__3);
  or or_8 (_8, condition2_3__2, condition2_5__3);
  or or_9 (_9, condition2_3__3, condition2_6__3, condition2_7__3);

  // Notes on the sheet:
  //   DECISION 2
endmodule

module decision3 (
  input  R1,
  input  G1,
  input  R2,
  input  G2,
  input  R3,
  input  G3,
  input  R4,
  input  G4,
  input  R5,
  input  G5,
  input  R6,
  input  G6,
  input  R7,
  input  G7,
  input  R8,
  input  G8,
  input  R9,
  input  G9,
  output _1,
  output _2,
  output _3,
  output _4,
  output _5,
  output _6,
  output _7,
  output _8,
  output _9
);

  wire nor_1_out, nor_2_out, nor_3_out, nor_4_out, nor_5_out, nor_6_out, nor_7_out, nor_8_out, nor_9_out;
  wire [3:0] priority_encoder_1_out;

  nor nor_1 (nor_1_out, R1, G1);
  nor nor_2 (nor_2_out, R3, G3);
  nor nor_3 (nor_3_out, R4, G4);
  nor nor_4 (nor_4_out, R5, G5);
  nor nor_5 (nor_5_out, R6, G6);
  nor nor_6 (nor_6_out, R7, G7);
  nor nor_7 (nor_7_out, R8, G8);
  nor nor_8 (nor_8_out, R9, G9);
  nor nor_9 (nor_9_out, R2, G2);
  Priority_Encoder #(.select(4)) priority_encoder_1 (
    .in0(nor_5_out), .in1(nor_3_out), .in2(nor_7_out), .in3(nor_9_out), .in4(nor_6_out), .in5(nor_2_out),
    .in6(nor_1_out), .in7(nor_8_out), .in8(nor_4_out), .in9(1'b0), .in10(1'b0), .in11(1'b0), .in12(1'b0),
    .in13(1'b0), .in14(1'b0), .in15(1'b0), .out(priority_encoder_1_out));  // open: gs, en_out, en_in
  Decoder #(.select(4)) decoder_1 (
    .out0(_6), .out1(_4), .out2(_8), .out3(_2), .out4(_7), .out5(_3), .out6(_1), .out7(_9), .out8(_5),
    .sel(priority_encoder_1_out));  // open: out9, out10, out11, out12, out13, out14, out15, en

  // Notes on the sheet:
  //   DECISION 3
endmodule

module Main (
);

  wire button_1_out, button_2_out, button_3_out, button_4_out, button_5_out, button_6_out, button_7_out,
       button_8_out, button_9_out, button_10_out, button_11_out, computerinput_1__1, computerinput_1__2,
       computerinput_1__3, computerinput_1__4, computerinput_1__5, computerinput_1__6, computerinput_1__7,
       computerinput_1__8, computerinput_1__9, d_ff_1_q, d_ff_2_q, d_ff_3_q, d_ff_4_q, d_ff_5_q, d_ff_6_q,
       d_ff_7_q, d_ff_8_q, d_ff_9_q, d_ff_10_q, d_ff_11_q, inputmodule_1__1_3, inputmodule_1__2_3,
       inputmodule_1__3_3, inputmodule_1__4_3, inputmodule_1__5_3, inputmodule_1__6_3, inputmodule_1__7_3,
       inputmodule_1__8_3, inputmodule_1__9_3, inputmodule_2__1_3, inputmodule_2__2_3, inputmodule_2__3_3,
       inputmodule_2__4_3, inputmodule_2__5_3, inputmodule_2__6_3, inputmodule_2__7_3, inputmodule_2__8_3,
       inputmodule_2__9_3, j_k_ff_1_q, j_k_ff_1_qn, not_1_out, not_2_out, not_3_out, or_1_out, or_2_out,
       or_3_out, or_4_out, or_5_out, userinput_1_output, userinput_2_output, userinput_3_output,
       userinput_4_output, userinput_5_output, userinput_6_output, userinput_7_output, userinput_8_output,
       userinput_9_output, wincondition_1_output, wincondition_2_output;

  Button button_1 (.out(button_1_out));
  Button button_2 (.out(button_2_out));
  Button button_3 (.out(button_3_out));
  userInput userinput_1 (
    .INPUT(button_1_out), .RESET(button_4_out), .BOT(inputmodule_2__1_3), .TURN(or_4_out),
    .OUTPUT(userinput_1_output));
  userInput userinput_2 (
    .INPUT(button_2_out), .RESET(button_4_out), .BOT(inputmodule_2__2_3), .TURN(or_4_out),
    .OUTPUT(userinput_2_output));
  Button button_4 (.out(button_4_out));
  Button button_5 (.out(button_5_out));
  Button button_6 (.out(button_6_out));
  Button button_7 (.out(button_7_out));
  Button button_8 (.out(button_8_out));
  userInput userinput_3 (
    .INPUT(button_3_out), .RESET(button_4_out), .BOT(inputmodule_2__3_3), .TURN(or_4_out),
    .OUTPUT(userinput_3_output));
  userInput userinput_4 (
    .INPUT(button_7_out), .RESET(button_4_out), .BOT(inputmodule_2__5_3), .TURN(or_4_out),
    .OUTPUT(userinput_4_output));
  userInput userinput_5 (
    .INPUT(button_8_out), .RESET(button_4_out), .BOT(inputmodule_2__6_3), .TURN(or_4_out),
    .OUTPUT(userinput_5_output));
  userInput userinput_6 (
    .INPUT(button_11_out), .RESET(button_4_out), .BOT(inputmodule_2__9_3), .TURN(or_4_out),
    .OUTPUT(userinput_6_output));
  userInput userinput_7 (
    .INPUT(button_10_out), .RESET(button_4_out), .BOT(inputmodule_2__8_3), .TURN(or_4_out),
    .OUTPUT(userinput_7_output));
  userInput userinput_8 (
    .INPUT(button_9_out), .RESET(button_4_out), .BOT(inputmodule_2__7_3), .TURN(or_4_out),
    .OUTPUT(userinput_8_output));
  or or_1 (or_1_out, userinput_1_output, userinput_2_output, userinput_3_output, userinput_4_output, userinput_5_output, userinput_6_output, userinput_7_output, userinput_8_output, userinput_9_output);
  Button button_9 (.out(button_9_out));
  Button button_10 (.out(button_10_out));
  Button button_11 (.out(button_11_out));
  userInput userinput_9 (
    .INPUT(button_6_out), .RESET(button_4_out), .BOT(inputmodule_2__4_3), .TURN(or_4_out),
    .OUTPUT(userinput_9_output));
  inputModule inputmodule_1 (
    ._1(button_1_out), ._2(button_2_out), ._3(button_3_out), ._4(button_6_out), ._5(button_7_out),
    ._6(button_8_out), ._7(button_9_out), ._8(button_10_out), ._9(button_11_out), .ENABLE(or_4_out),
    .RESET(button_4_out), ._1_2(inputmodule_2__1_3), ._2_2(inputmodule_2__2_3), ._3_2(inputmodule_2__3_3),
    ._4_2(inputmodule_2__4_3), ._5_2(inputmodule_2__5_3), ._6_2(inputmodule_2__6_3),
    ._7_2(inputmodule_2__7_3), ._8_2(inputmodule_2__8_3), ._9_2(inputmodule_2__9_3),
    ._1_3(inputmodule_1__1_3), ._2_3(inputmodule_1__2_3), ._3_3(inputmodule_1__3_3),
    ._4_3(inputmodule_1__4_3), ._5_3(inputmodule_1__5_3), ._6_3(inputmodule_1__6_3),
    ._7_3(inputmodule_1__7_3), ._8_3(inputmodule_1__8_3), ._9_3(inputmodule_1__9_3));
  or or_2 (or_2_out, or_1_out, button_5_out);
  J_K_Flip_Flop j_k_ff_1 (
    .J(or_1_out), .clk(or_2_out), .K(button_5_out), .Q(j_k_ff_1_q), .Qn(j_k_ff_1_qn), .reset(button_4_out));  // open: preset, en
  LED R1 (.in(inputmodule_1__1_3));
  LED G1 (.in(inputmodule_2__1_3));
  LED G2 (.in(inputmodule_2__2_3));
  LED R2 (.in(inputmodule_1__2_3));
  LED G3 (.in(inputmodule_2__3_3));
  LED R3 (.in(inputmodule_1__3_3));
  winCondition wincondition_1 (
    ._1(inputmodule_2__1_3), ._2(inputmodule_2__2_3), ._3(inputmodule_2__3_3), ._4(inputmodule_2__4_3),
    ._5(inputmodule_2__5_3), ._6(inputmodule_2__6_3), ._7(inputmodule_2__7_3), ._8(inputmodule_2__8_3),
    ._9(inputmodule_2__9_3), .OUTPUT(wincondition_1_output));
  winCondition wincondition_2 (
    ._1(inputmodule_1__1_3), ._2(inputmodule_1__2_3), ._3(inputmodule_1__3_3), ._4(inputmodule_1__4_3),
    ._5(inputmodule_1__5_3), ._6(inputmodule_1__6_3), ._7(inputmodule_1__7_3), ._8(inputmodule_1__8_3),
    ._9(inputmodule_1__9_3), .OUTPUT(wincondition_2_output));
  LED R4 (.in(inputmodule_1__4_3));
  LED R5 (.in(inputmodule_1__5_3));
  LED R6 (.in(inputmodule_1__6_3));
  computerInput computerinput_1 (
    .R1(inputmodule_1__1_3), .G1(inputmodule_2__1_3), .R2(inputmodule_1__2_3), .G2(inputmodule_2__2_3),
    .R3(inputmodule_1__3_3), .G3(inputmodule_2__3_3), .R4(inputmodule_1__4_3), .G4(inputmodule_2__4_3),
    .R5(inputmodule_1__5_3), .G5(inputmodule_2__5_3), .R6(inputmodule_1__6_3), .G6(inputmodule_2__6_3),
    .R7(inputmodule_1__7_3), .G7(inputmodule_2__7_3), .R8(inputmodule_1__8_3), .G8(inputmodule_2__8_3),
    .R9(inputmodule_1__9_3), .G9(inputmodule_2__9_3), ._1(computerinput_1__1), ._2(computerinput_1__2),
    ._3(computerinput_1__3), ._4(computerinput_1__4), ._5(computerinput_1__5), ._6(computerinput_1__6),
    ._7(computerinput_1__7), ._8(computerinput_1__8), ._9(computerinput_1__9));
  LED G4 (.in(inputmodule_2__4_3));
  LED G5 (.in(inputmodule_2__5_3));
  LED G6 (.in(inputmodule_2__6_3));
  LED R7 (.in(inputmodule_1__7_3));
  LED R8 (.in(inputmodule_1__8_3));
  LED R9 (.in(inputmodule_1__9_3));
  D_Flip_Flop d_ff_1 (
    .clk(wincondition_1_output), .D(1'b1), .Q(d_ff_1_q), .reset(button_4_out));  // open: Qn, preset, en
  D_Flip_Flop d_ff_2 (
    .clk(wincondition_2_output), .D(1'b1), .Q(d_ff_2_q), .reset(button_4_out));  // open: Qn, preset, en
  or or_3 (or_3_out, wincondition_1_output, wincondition_2_output);
  D_Flip_Flop d_ff_3 (
    .clk(button_5_out), .D(computerinput_1__1), .Q(d_ff_3_q), .en(not_1_out), .reset(button_4_out));  // open: Qn, preset
  D_Flip_Flop d_ff_4 (
    .clk(button_5_out), .D(computerinput_1__2), .Q(d_ff_4_q), .en(not_1_out), .reset(button_4_out));  // open: Qn, preset
  D_Flip_Flop d_ff_5 (
    .clk(button_5_out), .D(computerinput_1__3), .Q(d_ff_5_q), .en(not_1_out), .reset(button_4_out));  // open: Qn, preset
  D_Flip_Flop d_ff_6 (
    .clk(button_5_out), .D(computerinput_1__4), .Q(d_ff_6_q), .en(not_1_out), .reset(button_4_out));  // open: Qn, preset
  D_Flip_Flop d_ff_7 (
    .clk(button_5_out), .D(computerinput_1__5), .Q(d_ff_7_q), .en(not_1_out), .reset(button_4_out));  // open: Qn, preset
  D_Flip_Flop d_ff_8 (
    .clk(button_5_out), .D(computerinput_1__6), .Q(d_ff_8_q), .en(not_1_out), .reset(button_4_out));  // open: Qn, preset
  D_Flip_Flop d_ff_9 (
    .clk(button_5_out), .D(computerinput_1__7), .Q(d_ff_9_q), .en(not_1_out), .reset(button_4_out));  // open: Qn, preset
  D_Flip_Flop d_ff_10 (
    .clk(button_5_out), .D(computerinput_1__8), .Q(d_ff_10_q), .en(not_1_out), .reset(button_4_out));  // open: Qn, preset
  D_Flip_Flop d_ff_11 (
    .clk(button_5_out), .D(computerinput_1__9), .Q(d_ff_11_q), .en(not_1_out), .reset(button_4_out));  // open: Qn, preset
  or or_4 (or_4_out, j_k_ff_1_q, or_3_out);
  LED G7 (.in(inputmodule_2__7_3));
  LED G8 (.in(inputmodule_2__8_3));
  LED G9 (.in(inputmodule_2__9_3));
  LED led_1 (.in(d_ff_2_q));
  LED led_2 (.in(d_ff_1_q));
  not not_1 (not_1_out, or_5_out);
  LED led_3 (.in(not_2_out));
  LED led_4 (.in(not_3_out));
  inputModule inputmodule_2 (
    ._1(d_ff_3_q), ._2(d_ff_4_q), ._3(d_ff_5_q), ._4(d_ff_6_q), ._5(d_ff_7_q), ._6(d_ff_8_q), ._7(d_ff_9_q),
    ._8(d_ff_10_q), ._9(d_ff_11_q), .ENABLE(or_5_out), .RESET(button_4_out), ._1_2(1'b0), ._2_2(1'b0),
    ._3_2(1'b0), ._4_2(1'b0), ._5_2(1'b0), ._6_2(1'b0), ._7_2(1'b0), ._8_2(1'b0), ._9_2(1'b0),
    ._1_3(inputmodule_2__1_3), ._2_3(inputmodule_2__2_3), ._3_3(inputmodule_2__3_3),
    ._4_3(inputmodule_2__4_3), ._5_3(inputmodule_2__5_3), ._6_3(inputmodule_2__6_3),
    ._7_3(inputmodule_2__7_3), ._8_3(inputmodule_2__8_3), ._9_3(inputmodule_2__9_3));
  not not_2 (not_2_out, j_k_ff_1_qn);
  not not_3 (not_3_out, j_k_ff_1_q);
  or or_5 (or_5_out, j_k_ff_1_qn, or_3_out);

  // Notes on the sheet:
  //   MAIN CIRCUIT
  //   BOT INPUT
  //   INPUTS
  //   RESET
  //   OUTPUT
  //   WIN
  //   User Won
  //   Player Won
  //   TURN
  //   AUTONOMOUS TIC-TAC-TOE BOT
  //   S1-T8
  //   PRAHAS G R   231CS142
  //   M VINEET NAYAK   231CS132
  //   NISCHAL BASAVARAJU   231CS139
  //   INSTRUCTIONS
  //   1. Go to 'Simulate', then click on 'Ticks Enabled'
  //   2. Click on RESET to ensure none of the LED's are glowing.
  //   3. Select the button of your choice to make a move.
  //   4. Click on the 'BOT INPUT' button to make the bot play.
  //   6. At the end of the game, click on the RESET button.
  //   5. The 'TURN' LEDs show whose turn it is, and the 'WIN' LEDs indicate the winner if any.
endmodule

module inputModule (
  input  RESET,
  input  ENABLE,
  input  _1,
  input  _2,
  input  _3,
  input  _4,
  input  _5,
  input  _6,
  input  _7,
  input  _8,
  input  _9,
  input  _1_2,
  input  _2_2,
  input  _3_2,
  input  _4_2,
  input  _5_2,
  input  _6_2,
  input  _7_2,
  input  _8_2,
  input  _9_2,
  output _1_3,
  output _2_3,
  output _3_3,
  output _4_3,
  output _5_3,
  output _6_3,
  output _7_3,
  output _8_3,
  output _9_3
);

  wire multiplexer_1_out, multiplexer_2_out, multiplexer_3_out, multiplexer_4_out, multiplexer_5_out,
       multiplexer_6_out, multiplexer_7_out, multiplexer_8_out, multiplexer_9_out, not_1_out, not_2_out,
       not_3_out, not_4_out, not_5_out, not_6_out, not_7_out, not_8_out, not_9_out;

  Multiplexer multiplexer_1 (.in0(_1), .in1(1'b0), .out(multiplexer_1_out), .sel(ENABLE));  // open: en
  Multiplexer multiplexer_2 (.in0(_2), .in1(1'b0), .out(multiplexer_2_out), .sel(ENABLE));  // open: en
  Multiplexer multiplexer_3 (.in0(_3), .in1(1'b0), .out(multiplexer_3_out), .sel(ENABLE));  // open: en
  Multiplexer multiplexer_4 (.in0(_4), .in1(1'b0), .out(multiplexer_4_out), .sel(ENABLE));  // open: en
  Multiplexer multiplexer_5 (.in0(_5), .in1(1'b0), .out(multiplexer_5_out), .sel(ENABLE));  // open: en
  Multiplexer multiplexer_6 (.in0(_6), .in1(1'b0), .out(multiplexer_6_out), .sel(ENABLE));  // open: en
  Multiplexer multiplexer_7 (.in0(_7), .in1(1'b0), .out(multiplexer_7_out), .sel(ENABLE));  // open: en
  Multiplexer multiplexer_8 (.in0(_8), .in1(1'b0), .out(multiplexer_8_out), .sel(ENABLE));  // open: en
  Multiplexer multiplexer_9 (.in0(_9), .in1(1'b0), .out(multiplexer_9_out), .sel(ENABLE));  // open: en
  D_Flip_Flop d_ff_1 (.clk(multiplexer_1_out), .D(1'b1), .Q(_1_3), .en(not_2_out), .reset(RESET));  // open: Qn, preset
  D_Flip_Flop d_ff_2 (.clk(multiplexer_2_out), .D(1'b1), .Q(_2_3), .en(not_3_out), .reset(RESET));  // open: Qn, preset
  D_Flip_Flop d_ff_3 (.clk(multiplexer_3_out), .D(1'b1), .Q(_3_3), .en(not_4_out), .reset(RESET));  // open: Qn, preset
  D_Flip_Flop d_ff_4 (.clk(multiplexer_4_out), .D(1'b1), .Q(_4_3), .en(not_1_out), .reset(RESET));  // open: Qn, preset
  D_Flip_Flop d_ff_5 (.clk(multiplexer_5_out), .D(1'b1), .Q(_5_3), .en(not_7_out), .reset(RESET));  // open: Qn, preset
  D_Flip_Flop d_ff_6 (.clk(multiplexer_6_out), .D(1'b1), .Q(_6_3), .en(not_5_out), .reset(RESET));  // open: Qn, preset
  D_Flip_Flop d_ff_7 (.clk(multiplexer_7_out), .D(1'b1), .Q(_7_3), .en(not_6_out), .reset(RESET));  // open: Qn, preset
  D_Flip_Flop d_ff_8 (.clk(multiplexer_8_out), .D(1'b1), .Q(_8_3), .en(not_8_out), .reset(RESET));  // open: Qn, preset
  D_Flip_Flop d_ff_9 (.clk(multiplexer_9_out), .D(1'b1), .Q(_9_3), .en(not_9_out), .reset(RESET));  // open: Qn, preset
  not not_1 (not_1_out, _4_2);
  not not_2 (not_2_out, _1_2);
  not not_3 (not_3_out, _2_2);
  not not_4 (not_4_out, _3_2);
  not not_5 (not_5_out, _6_2);
  not not_6 (not_6_out, _7_2);
  not not_7 (not_7_out, _5_2);
  not not_8 (not_8_out, _8_2);
  not not_9 (not_9_out, _9_2);

  // Notes on the sheet:
  //   INPUT MODULE
endmodule

module computerInput (
  input  R1,
  input  G1,
  input  R2,
  input  G2,
  input  R3,
  input  G3,
  input  R4,
  input  G4,
  input  R5,
  input  G5,
  input  R6,
  input  G6,
  input  R7,
  input  G7,
  input  R8,
  input  G8,
  input  R9,
  input  G9,
  output _1,
  output _2,
  output _3,
  output _4,
  output _5,
  output _6,
  output _7,
  output _8,
  output _9
);

  wire and_1_out, and_2_out, and_3_out, and_4_out, and_5_out, and_6_out, and_7_out, and_8_out, and_9_out,
       and_10_out, and_11_out, and_12_out, and_13_out, and_14_out, and_15_out, and_16_out, and_17_out,
       and_18_out, decision1_1__1, decision1_1__2, decision1_1__3, decision1_1__4, decision1_1__5,
       decision1_1__6, decision1_1__7, decision1_1__8, decision1_1__9, decision2_1__1, decision2_1__2,
       decision2_1__3, decision2_1__4, decision2_1__5, decision2_1__6, decision2_1__7, decision2_1__8,
       decision2_1__9, decision3_1__1, decision3_1__2, decision3_1__3, decision3_1__4, decision3_1__5,
       decision3_1__6, decision3_1__7, decision3_1__8, decision3_1__9, decoder_1_out7, decoder_1_out8,
       decoder_1_out9, decoder_1_out10, decoder_1_out11, decoder_1_out12, decoder_1_out13, decoder_1_out14,
       decoder_1_out15, decoder_2_out7, decoder_2_out8, decoder_2_out9, decoder_2_out10, decoder_2_out11,
       decoder_2_out12, decoder_2_out13, decoder_2_out14, decoder_2_out15, decoder_3_out7, decoder_3_out8,
       decoder_3_out9, decoder_3_out10, decoder_3_out11, decoder_3_out12, decoder_3_out13, decoder_3_out14,
       decoder_3_out15, nor_1_out, nor_2_out;
  wire [3:0] priority_encoder_1_out, priority_encoder_2_out, priority_encoder_3_out;

  decision1 decision1_1 (
    .R1(R1), .G1(G1), .R2(R2), .G2(G2), .R3(R3), .G3(G3), .R4(R4), .G4(G4), .R5(R5), .G5(G5), .R6(R6),
    .G6(G6), .R7(R7), .G7(G7), .R8(R8), .G8(G8), .R9(R9), .G9(G9), ._1(decision1_1__1), ._2(decision1_1__2),
    ._3(decision1_1__3), ._4(decision1_1__4), ._5(decision1_1__5), ._6(decision1_1__6), ._7(decision1_1__7),
    ._8(decision1_1__8), ._9(decision1_1__9));
  decision2 decision2_1 (
    .R1(R1), .G1(G1), .R2(R2), .G2(G2), .R3(R3), .G3(G3), .R4(R4), .G4(G4), .R5(R5), .G5(G5), .R6(R6),
    .G6(G6), .R7(R7), .G7(G7), .R8(R8), .G8(G8), .R9(R9), .G9(G9), ._1(decision2_1__1), ._2(decision2_1__2),
    ._3(decision2_1__3), ._4(decision2_1__4), ._5(decision2_1__5), ._6(decision2_1__6), ._7(decision2_1__7),
    ._8(decision2_1__8), ._9(decision2_1__9));
  decision3 decision3_1 (
    .R1(R1), .G1(G1), .R2(R2), .G2(G2), .R3(R3), .G3(G3), .R4(R4), .G4(G4), .R5(R5), .G5(G5), .R6(R6),
    .G6(G6), .R7(R7), .G7(G7), .R8(R8), .G8(G8), .R9(R9), .G9(G9), ._1(decision3_1__1), ._2(decision3_1__2),
    ._3(decision3_1__3), ._4(decision3_1__4), ._5(decision3_1__5), ._6(decision3_1__6), ._7(decision3_1__7),
    ._8(decision3_1__8), ._9(decision3_1__9));
  Priority_Encoder #(.select(4)) priority_encoder_1 (
    .in0(1'b1), .in1(1'b1), .in2(1'b1), .in3(1'b1), .in4(1'b1), .in5(1'b1), .in6(1'b1), .in7(decision1_1__1),
    .in8(decision1_1__2), .in9(decision1_1__3), .in10(decision1_1__4), .in11(decision1_1__5),
    .in12(decision1_1__6), .in13(decision1_1__7), .in14(decision1_1__8), .in15(decision1_1__9),
    .out(priority_encoder_1_out));  // open: gs, en_out, en_in
  Decoder #(.select(4)) decoder_1 (
    .out7(decoder_1_out7), .out8(decoder_1_out8), .out9(decoder_1_out9), .out10(decoder_1_out10),
    .out11(decoder_1_out11), .out12(decoder_1_out12), .out13(decoder_1_out13), .out14(decoder_1_out14),
    .out15(decoder_1_out15), .sel(priority_encoder_1_out));  // open: out0, out1, out2, out3, out4, out5, out6, en
  Priority_Encoder #(.select(4)) priority_encoder_2 (
    .in0(1'b1), .in1(1'b1), .in2(1'b1), .in3(1'b1), .in4(1'b1), .in5(1'b1), .in6(1'b1), .in7(decision2_1__1),
    .in8(decision2_1__2), .in9(decision2_1__3), .in10(decision2_1__4), .in11(decision2_1__5),
    .in12(decision2_1__6), .in13(decision2_1__7), .in14(decision2_1__8), .in15(decision2_1__9),
    .out(priority_encoder_2_out));  // open: gs, en_out, en_in
  Decoder #(.select(4)) decoder_2 (
    .out7(decoder_2_out7), .out8(decoder_2_out8), .out9(decoder_2_out9), .out10(decoder_2_out10),
    .out11(decoder_2_out11), .out12(decoder_2_out12), .out13(decoder_2_out13), .out14(decoder_2_out14),
    .out15(decoder_2_out15), .sel(priority_encoder_2_out));  // open: out0, out1, out2, out3, out4, out5, out6, en
  Priority_Encoder #(.select(4)) priority_encoder_3 (
    .in0(1'b1), .in1(1'b1), .in2(1'b1), .in3(1'b1), .in4(1'b1), .in5(1'b1), .in6(1'b1), .in7(decision3_1__1),
    .in8(decision3_1__2), .in9(decision3_1__3), .in10(decision3_1__4), .in11(decision3_1__5),
    .in12(decision3_1__6), .in13(decision3_1__7), .in14(decision3_1__8), .in15(decision3_1__9),
    .out(priority_encoder_3_out));  // open: gs, en_out, en_in
  Decoder #(.select(4)) decoder_3 (
    .out7(decoder_3_out7), .out8(decoder_3_out8), .out9(decoder_3_out9), .out10(decoder_3_out10),
    .out11(decoder_3_out11), .out12(decoder_3_out12), .out13(decoder_3_out13), .out14(decoder_3_out14),
    .out15(decoder_3_out15), .sel(priority_encoder_3_out));  // open: out0, out1, out2, out3, out4, out5, out6, en
  nor nor_1 (nor_1_out, decoder_1_out7, decoder_1_out8, decoder_1_out9, decoder_1_out10, decoder_1_out11, decoder_1_out12, decoder_1_out13, decoder_1_out14, decoder_1_out15);
  nor nor_2 (nor_2_out, decoder_2_out7, decoder_2_out8, decoder_2_out9, decoder_2_out10, decoder_2_out11, decoder_2_out12, decoder_2_out13, decoder_2_out14, decoder_2_out15);
  and and_1 (and_1_out, decoder_2_out7, nor_1_out);
  and and_2 (and_2_out, decoder_3_out7, nor_1_out, nor_2_out);
  and and_3 (and_3_out, nor_1_out, decoder_2_out8);
  and and_4 (and_4_out, nor_1_out, nor_2_out, decoder_3_out8);
  and and_5 (and_5_out, nor_1_out, decoder_2_out9);
  and and_6 (and_6_out, nor_1_out, nor_2_out, decoder_3_out9);
  and and_7 (and_7_out, nor_1_out, decoder_2_out10);
  and and_8 (and_8_out, nor_1_out, nor_2_out, decoder_3_out10);
  and and_9 (and_9_out, nor_1_out, decoder_2_out11);
  and and_10 (and_10_out, nor_1_out, nor_2_out, decoder_3_out11);
  and and_11 (and_11_out, nor_1_out, decoder_2_out12);
  and and_12 (and_12_out, nor_1_out, decoder_3_out12, nor_2_out);
  and and_13 (and_13_out, nor_1_out, decoder_2_out13);
  and and_14 (and_14_out, nor_1_out, nor_2_out, decoder_3_out13);
  and and_15 (and_15_out, nor_1_out, decoder_2_out14);
  and and_16 (and_16_out, nor_1_out, nor_2_out, decoder_3_out14);
  and and_17 (and_17_out, nor_1_out, decoder_2_out15);
  and and_18 (and_18_out, nor_1_out, nor_2_out, decoder_3_out15);
  or or_1 (_1, and_1_out, and_2_out, decoder_1_out7);
  or or_2 (_2, and_3_out, and_4_out, decoder_1_out8);
  or or_3 (_3, and_5_out, and_6_out, decoder_1_out9);
  or or_4 (_4, and_7_out, and_8_out, decoder_1_out10);
  or or_5 (_5, and_9_out, and_10_out, decoder_1_out11);
  or or_6 (_6, and_11_out, and_12_out, decoder_1_out12);
  or or_7 (_7, and_13_out, and_14_out, decoder_1_out13);
  or or_8 (_8, and_15_out, and_16_out, decoder_1_out14);
  or or_9 (_9, and_17_out, and_18_out, decoder_1_out15);

  // Notes on the sheet:
  //   COMPUTER INPUT
endmodule

module winCondition (
  input  _1,
  input  _2,
  input  _3,
  input  _4,
  input  _5,
  input  _6,
  input  _7,
  input  _8,
  input  _9,
  output OUTPUT
);

  wire and_1_out, and_2_out, and_3_out, and_4_out, and_5_out, and_6_out, and_7_out, and_8_out;

  and and_1 (and_1_out, _1, _2, _3);
  and and_2 (and_2_out, _2, _5, _8);
  and and_3 (and_3_out, _3, _5, _7);
  and and_4 (and_4_out, _1, _7, _4);
  and and_5 (and_5_out, _4, _6, _5);
  and and_6 (and_6_out, _3, _6, _9);
  and and_7 (and_7_out, _1, _5, _9);
  and and_8 (and_8_out, _7, _9, _8);
  or or_1 (OUTPUT, and_1_out, and_2_out, and_3_out, and_4_out, and_5_out, and_6_out, and_7_out, and_8_out);

  // Notes on the sheet:
  //   WIN CONDITION
endmodule

module userInput (
  input  BOT,
  input  INPUT,
  input  RESET,
  input  TURN,
  output OUTPUT
);

  wire and_1_out, clock_1_out, d_ff_1_q, d_ff_1_qn, d_ff_2_q, d_ff_3_q, not_1_out, not_2_out, not_3_out;

  Clock clock_1 (.out(clock_1_out));
  and and_1 (and_1_out, INPUT, d_ff_1_qn);
  D_Flip_Flop d_ff_1 (.clk(and_1_out), .D(1'b1), .Q(d_ff_1_q), .Qn(d_ff_1_qn), .reset(RESET));  // open: preset, en
  D_Flip_Flop d_ff_2 (.clk(clock_1_out), .D(d_ff_1_q), .Q(d_ff_2_q), .reset(RESET));  // open: Qn, preset, en
  D_Flip_Flop d_ff_3 (.clk(clock_1_out), .D(d_ff_2_q), .Q(d_ff_3_q), .reset(RESET));  // open: Qn, preset, en
  not not_1 (not_1_out, BOT);
  not not_2 (not_2_out, d_ff_3_q);
  not not_3 (not_3_out, TURN);
  and and_2 (OUTPUT, not_1_out, not_2_out, d_ff_1_q, not_3_out);

  // Notes on the sheet:
  //   USER INPUT
endmodule
