// Logisim project Scaled Down.circ as structural Verilog: 3 circuits, main circuit main
module main (
  input  in_1,
  input  in_2,
  input  in_3,
  input  in_4
);

  wire and_1_out, and_2_out, and_3_out, Bot_out, BotInput_b1, BotInput_b3, BotInput_b4, Reset_out,
       User_Check__1, User_Check__3, User_Check__4;

  Button Bot (.out(Bot_out));
  Button Reset (.out(Reset_out));
  Bot_Input BotInput (
    .P3(in_3), .Clock(Bot_out), .Reset(Reset_out), .B4(BotInput_b4), .B3(BotInput_b3), .B1(BotInput_b1));
  User_Check User_Check (
    .P4(in_4), .B4(BotInput_b4), .P3(in_3), .B3(BotInput_b3), .P1(in_1), .B1(BotInput_b1),
    ._4(User_Check__4), ._3(User_Check__3), ._1(User_Check__1));
  LED led_1 (.in(User_Check__1));
  LED led_2 (.in(User_Check__3));
  LED led_3 (.in(BotInput_b1));
  LED led_4 (.in(BotInput_b3));
  LED led_5 (.in(in_2));
  LED led_6 ();  // open: in
  LED led_7 (.in(User_Check__4));
  LED led_8 (.in(BotInput_b4));
  and and_1 (and_1_out, BotInput_b4, BotInput_b3);
  and and_2 (and_2_out, BotInput_b4, User_Check__3);
  and and_3 (and_3_out, User_Check__1, in_2);
  LED Bot_2 (.in(and_1_out));
  LED User (.in(and_3_out));
  LED Tie (.in(and_2_out));

  // Notes on the sheet:
  //   WIN SITUATION
endmodule

module Bot_Input (
  input  P3,
  input  Clock,
  input  Reset,
  output B4,
  output B3,
  output B1
);

  wire and_1_out, and_2_out, not_1_out;

  D_Flip_Flop d_ff_1 (.clk(Clock), .D(1'b1), .Q(B4), .reset(Reset));  // open: Qn, preset, en
  D_Flip_Flop d_ff_2 (.clk(Clock), .D(and_1_out), .Q(B3), .reset(Reset));  // open: Qn, preset, en
  and and_1 (and_1_out, B4, not_1_out);
  and and_2 (and_2_out, B4, P3);
  D_Flip_Flop d_ff_3 (.clk(Clock), .D(and_2_out), .Q(B1), .reset(Reset));  // open: Qn, preset, en
  not not_1 (not_1_out, P3);
endmodule

module User_Check (
  input  P4,
  input  B4,
  input  P3,
  input  B3,
  input  P1,
  input  B1,
  output _4,
  output _3,
  output _1
);

  wire not_1_out, not_2_out, not_3_out;

  not not_1 (not_1_out, B4);
  not not_2 (not_2_out, B3);
  not not_3 (not_3_out, B1);
  and and_1 (_4, P4, not_1_out);
  and and_2 (_3, P3, not_2_out);
  and and_3 (_1, P1, not_3_out);
endmodule
